# Fritzing sketch SchemaBranchements (saved by Fritzing 0.9.2b)
breadboards: 1

parts:
  Composant1 = Arduino Uno (Rev3)
  S1 = Pushbutton [package="[THT]"]
  S2 = Pushbutton [package="[THT]"]
  S3 = Pushbutton [package="[THT]"]
  S4 = Pushbutton [package="[THT]"]

nets:
  N1: Composant1.GND, S1.Pin_1, S1.Pin_2, S2.Pin_1, S2.Pin_2, S3.Pin_1, S3.Pin_2, S4.Pin_1, S4.Pin_2
  N2: Composant1.D2, S1.Pin_3, S1.Pin_4
  N3: Composant1.D3_PWM, S2.Pin_3, S2.Pin_4
  N4: Composant1.D4, S3.Pin_3, S3.Pin_4
  N5: Composant1.D5_PWM, S4.Pin_3, S4.Pin_4
